# Fritzing sketch IntervalometroSketchFritizing (saved by Fritzing 0.9.6b)
breadboards: 1

parts:
  Componente1 = Arduino Nano (Rev3.0)
  LCD1 = LCD screen
  LED1 = smd LED [color="Red (633nm)" package="0805 [SMD]"]  # not connected
  LED2 = smd LED [color="Orange (612nm)" package="0805 [SMD]"]  # not connected
  S1 = Momentary Switch [package=ksa_sealed_tac_switch]  # not connected
  S2 = Momentary Switch [package=ksa_sealed_tac_switch]  # not connected
  S3 = Momentary Switch [package=ksa_sealed_tac_switch]  # not connected
  R1 = Resistor [tolerance=±5% resistance=10k package="0402 [SMD]"]  # not connected
  R2 = Resistor [tolerance=±5% resistance=10k package="0402 [SMD]"]  # not connected

nets:
  N1: Componente1.A5, LCD1.V0
  N2: Componente1.A4, LCD1.RS

notes:
  A5 / SCL
  A4/ SDA / SCA
  Usar LCD I2C con 4 conectores
  Libreria LiquidCrystal_I2C
